# Fritzing sketch Diagram (saved by Fritzing 0.9.3b)
perfboards: 1

parts:
  Raspberry_Pi_2 = Raspberry Pi 3 [part_number=RPI-3-V1.2]
  Arduino_Mega = Arduino Mega ADK (Rev3)
  Pololu_A2 = Pololu A4988 [package=SO16]
  Pololu_A3 = Pololu A4988 [package=SO16]
  Pololu_A4 = Pololu A4988 [package=SO16]
  Pololu_A5 = Pololu A4988 [package=SO16]
  Pololu_A1 = Pololu A4988 [package=SO16]
  M1 = Stepper Motor - Bipolar
  J1 = Camdenboss CTB0158-4 [part_number=CTB0158-4 package=THT]
  M2 = Stepper Motor - Bipolar
  M3 = Stepper Motor - Bipolar
  M4 = Stepper Motor - Bipolar
  M5 = Stepper Motor - Bipolar
  30A = DC Power [voltage=12V]
  Q1 = npn-Powertransistor [package="TO220 [THT]"]
  S3 = Pushbutton [package="[SMD]"]
  S4 = Pushbutton [package="[SMD]"]
  S5 = Pushbutton [package="[SMD]"]
  S6 = Pushbutton [package="[SMD]"]
  R1 = Resistor [tolerance=±5% resistance=10k package=THT]  # not connected
  R2 = Resistor [tolerance=±5% resistance=10k package=THT]
  R3 = Resistor [tolerance=±5% resistance=10k package=THT]  # not connected
  R4 = Resistor [tolerance=±5% resistance=10k package=THT]
  Q2 = npn-Powertransistor [package="TO220 [THT]"]

nets:
  N1: Raspberry_Pi_2.GPIO2, Arduino_Mega.D20/SDA
  N2: Raspberry_Pi_2.GPIO3, Arduino_Mega.D21/SCL
  N3: Arduino_Mega.D13_PWM, Q1.collector
  N4: Arduino_Mega.D12_PWM, Q2.collector
  N5: Arduino_Mega.D11_PWM, Pololu_A2.DIR
  N6: Arduino_Mega.D10_PWM, Pololu_A2.STEP
  N7: Arduino_Mega.D9_PWM, Pololu_A5.DIR
  N8: Arduino_Mega.D8_PWM, Pololu_A5.STEP
  N9: Arduino_Mega.5V, J1.terminal_3
  N10: Arduino_Mega.GND, J1.terminal_4, R2.Pin_0, R4.Pin_0
  N11: Arduino_Mega.D2_PWM, Pololu_A3.STEP
  N12: Arduino_Mega.D3_PWM, Pololu_A3.DIR
  N13: Arduino_Mega.D4_PWM, Pololu_A4.STEP
  N14: Arduino_Mega.D5_PWM, Pololu_A4.DIR
  N15: Arduino_Mega.D6_PWM, Pololu_A1.STEP
  N16: Arduino_Mega.D7_PWM, Pololu_A1.DIR
  N17: Arduino_Mega.D22, S6.Pin_3
  N18: Arduino_Mega.D24, S3.Pin_3, S3.Pin_4
  N19: Arduino_Mega.D26, S4.Pin_3, S4.Pin_4
  N20: Arduino_Mega.D28, S5.Pin_3
  N21: Pololu_A2.MS1, Pololu_A2.MS2, Pololu_A2.MS3, Pololu_A2.VDD
  N22: Pololu_A2.RESET, Pololu_A2.SLEEP
  N23: Pololu_A2.1B, M2.A
  N24: Pololu_A2.1A, M2.C
  N25: Pololu_A2.2A, M2.B
  N26: Pololu_A2.2B, M2.D
  N27: Pololu_A2.VMOT, J1.pin1, 30A.V+
  N28: Pololu_A3.MS1, Pololu_A3.MS2, Pololu_A3.MS3, Pololu_A3.VDD
  N29: Pololu_A3.RESET, Pololu_A3.SLEEP
  N30: Pololu_A3.1B, M3.A
  N31: Pololu_A3.1A, M3.C
  N32: Pololu_A3.2A, M3.B
  N33: Pololu_A3.2B, M3.D
  N34: Pololu_A4.MS1, Pololu_A4.MS2, Pololu_A4.MS3, Pololu_A4.VDD
  N35: Pololu_A4.RESET, Pololu_A4.SLEEP
  N36: Pololu_A4.1B, M4.A
  N37: Pololu_A4.1A, M4.C
  N38: Pololu_A4.2A, M4.B
  N39: Pololu_A4.2B, M4.D
  N40: Pololu_A5.MS1, Pololu_A5.MS2, Pololu_A5.MS3, Pololu_A5.VDD
  N41: Pololu_A5.RESET, Pololu_A5.SLEEP
  N42: Pololu_A5.GND#8, J1.pin4
  N43: Pololu_A5.1B, M5.A
  N44: Pololu_A5.1A, M5.C
  N45: Pololu_A5.2A, M5.B
  N46: Pololu_A5.2B, M5.D
  N47: Pololu_A1.MS1, Pololu_A1.MS2, Pololu_A1.MS3, Pololu_A1.VDD
  N48: Pololu_A1.RESET, Pololu_A1.SLEEP
  N49: Pololu_A1.1B, M1.A
  N50: Pololu_A1.1A, M1.C
  N51: Pololu_A1.2A, M1.B
  N52: Pololu_A1.2B, M1.D
  N53: J1.pin2, 30A.V-

notes:
  12V 30A PS
  +
  -
  Vin
  Gnd
  Vout
  12V DC Water Pump
  12V Pump
  Endstops
  SMAKN DC/DC convertor
  12v => 5v/3a
  10kΩ
  12V DC Vacuum Pump
